// Digital circuit 1024x768.dig as structural Verilog
module _1024x768 (
  input  clk,
  input  en,
  input  clr,
  output [9:0] Y,
  output [9:0] X,
  output ovf
);

  wire and_1_out, comparator_1_lt, comparator_2_eq, or_1_out, or_2_out;

  or or_1 (or_1_out, clr, ovf);
  or or_2 (or_2_out, clr, comparator_2_eq);
  Counter #(.Bits(10)) u_Y (.en(and_1_out), .C(clk), .clr(or_1_out), .out(Y));  // open: ovf
  Counter #(.Bits(10)) u_X (.en(en), .C(clk), .clr(or_2_out), .out(X));  // open: ovf
  Comparator #(.Bits(10)) comparator_1 (.a(Y), .b(10'h2ff), .eq(ovf), .lt(comparator_1_lt));  // open: gt
  Comparator #(.Bits(10)) comparator_2 (.a(X), .b({10{1'b1}}), .eq(comparator_2_eq));  // open: gt, lt
  and and_1 (and_1_out, comparator_1_lt, comparator_2_eq);

  // Notes on the sheet:
  //   clk: Hz: 2147483647
endmodule
