// Digital circuit VGA_SYNC_JARVI-1024x768.dig as structural Verilog
// Designed for a 
// 65MHz clock.
// Generates 
// 1024x768@60Hz
// {{de Ausgelegt für einen 
// 25.175MHz Takt.
// Erzeugt
// 640x480@60Hz}}
module VGA_SYNC_JARVI_1024x768 (
  input  Clock,
  output [10:0] X,
  output [9:0] Y,
  output oe,
  output H_sync,
  output V_sync
);

  wire and_1_out, jk_ff_2_q, jken_1_p5, visible_column__1_eq, visible_column__plus__front_porch__1_eq,
       visible_column__plus__front_porch__plus__sync_pulse__1_eq, visible_row__1_eq,
       visible_row__plus__front_porch___1_eq, visible_row__plus_front_porch__plus__sync_width___1_eq,
       whole_frame__1_eq, whole_row__1_eq;

  Counter #(.Bits(11)) h_cnt (.en(1'b1), .C(Clock), .clr(whole_row__1_eq), .out(X));  // open: ovf
  Comparator #(.Bits(11)) visible_row__plus__front_porch___1 (
    .a(X), .b(11'h417), .eq(visible_row__plus__front_porch___1_eq));  // open: gt, lt
  Comparator #(.Bits(11)) visible_row__plus_front_porch__plus__sync_width___1 (
    .a(X), .b(11'h49f), .eq(visible_row__plus_front_porch__plus__sync_width___1_eq));  // open: gt, lt
  Comparator #(.Bits(11)) visible_row__1 (.a(X), .b(11'h3ff), .eq(visible_row__1_eq));  // open: gt, lt
  Comparator #(.Bits(11)) whole_row__1 (.a(X), .b(11'h53f), .eq(whole_row__1_eq));  // open: gt, lt
  and and_1 (and_1_out, whole_row__1_eq, whole_frame__1_eq);
  JK_FF jk_ff_1 (
    .J(visible_row__plus__front_porch___1_eq), .C(Clock),
    .K(visible_row__plus_front_porch__plus__sync_width___1_eq), .nQ(H_sync));  // open: Q
  JK_FF #(.Default(1)) jk_ff_2 (.J(whole_row__1_eq), .C(Clock), .K(visible_row__1_eq), .Q(jk_ff_2_q));  // open: nQ
  Counter #(.Bits(10)) v_cnt (.en(whole_row__1_eq), .C(Clock), .clr(and_1_out), .out(Y));  // open: ovf
  Comparator #(.Bits(10)) whole_frame__1 (.a(Y), .b(10'h325), .eq(whole_frame__1_eq));  // open: gt, lt
  Comparator #(.Bits(10)) visible_column__1 (.a(Y), .b(10'h2ff), .eq(visible_column__1_eq));  // open: gt, lt
  Comparator #(.Bits(10)) visible_column__plus__front_porch__1 (
    .a(Y), .b(10'h302), .eq(visible_column__plus__front_porch__1_eq));  // open: gt, lt
  Comparator #(.Bits(10)) visible_column__plus__front_porch__plus__sync_pulse__1 (
    .a(Y), .b(10'h308), .eq(visible_column__plus__front_porch__plus__sync_pulse__1_eq));  // open: gt, lt
  // JKen jken_1: pin names not known; wires that end beside it: whole_row__1_eq, whole_frame__1_eq, Clock, visible_column__1_eq, jken_1_p5
  // JKen jken_2: pin names not known; wires that end beside it: whole_row__1_eq, visible_column__plus__front_porch__1_eq, Clock, visible_column__plus__front_porch__plus__sync_pulse__1_eq, V_sync
  and and_2 (oe, jk_ff_2_q, jken_1_p5);

  // Other names for the same wires on the sheet: C = Clock

  // Notes on the sheet:
  //   X: The x coordinate of visible pixel.
  //   Is valid only if oe is high.
  //   {{de Die x-Koordinate des sichtbaren Pixels.
  //   Nur gültig, wenn oe auf HIGH gesetzt ist.}}
  //   Y: The y coordinate of visible pixel.
  //   Is valid only if oe is high.
  //   oe: If oe is high the x- and y-coordinates are valid and 
  //   a visible pixel is to output.
  //   {{de Wenn oe HIGH ist, sind x- und y-Koordinate
  //   gültig, und es muss ein Pixel ausgegeben werden.}}
  //   H_sync: The horizontal sync signal. Is low active.
  //   {{de Das horizontale sync-Signal. Ist Active Low}}
  //   V_sync: The vertical sync signal. Is low active.
  //   {{de Das vertikale sync-Signal. Ist Active Low}}
  //   Clock: pin W5, Hz: 65000000
  //   Designed for a 
  //   65MHz clock.
  //   Generates 
  //   1024x768@60Hz
endmodule

/* Test case H-Sync:
C H-sync oe X

repeat(799) C x x  x

loop (n,3)
loop (p,800)
C  ((p<640+16)|(p>=640+16+96)) (p<640) (p)
end loop
end loop
*/

/* Test case X-Y:
C X Y oe H-sync V-sync

# skip first image
repeat(419999) C x x x x x

# test second image coordiates
loop (i,2)
  loop (y,525)
    loop (x,800)
      C (x) (y) ((x<640)&(y<480)) ((x<640+16)|(x>=640+16+96)) ((y<480+10)|(y>=480+12))
    end loop
  end loop
end loop
*/
