// Digital circuit heart-animation-graphic-ram.dig as structural Verilog
module heart_animation_graphic_ram (
  input  SW0,
  input  SW1,
  input  SW2,
  input  SW3,
  input  SW4,
  input  SW5,
  input  SW6,
  input  SW7,
  input  SW8,
  input  SW9,
  input  SW10,
  input  SW11,
  input  Clock,
  output R0,
  output G0,
  output B0,
  output R1,
  output G1,
  output B1,
  output R2,
  output G2,
  output B2,
  output R3,
  output G3,
  output B3,
  output H_sync,
  output V_sync
);

  wire counter_1_ovf, decoder_1_out_0, decoder_1_out_1, decoder_1_out_2, decoder_1_out_3, or_1_out,
       vga_sync_jarvi_1024x768_1_h_sync, vga_sync_jarvi_1024x768_1_oe, vga_sync_jarvi_1024x768_1_v_sync;
  wire [1:0] counter_2_out, graphiccard_1_d;
  wire [4:0] vga_sync_jarvi_1024x768_1_x, vga_sync_jarvi_1024x768_1_y;
  wire [9:4] graphiccard_1_d_2;
  wire [9:5] vga_sync_jarvi_1024x768_1_y_2;
  wire [10:5] vga_sync_jarvi_1024x768_1_x_2;

  Counter #(.Bits(20)) counter_1 (.en(1'b1), .C(Clock), .clr(1'b0), .ovf(counter_1_ovf));  // open: out
  VGA_SYNC_JARVI_1024x768 vga_sync_jarvi_1024x768_1 (
    .Clock(Clock), .X({vga_sync_jarvi_1024x768_1_x_2, vga_sync_jarvi_1024x768_1_x}),
    .Y({vga_sync_jarvi_1024x768_1_y_2, vga_sync_jarvi_1024x768_1_y}), .oe(vga_sync_jarvi_1024x768_1_oe),
    .H_sync(vga_sync_jarvi_1024x768_1_h_sync), .V_sync(vga_sync_jarvi_1024x768_1_v_sync));
  Counter #(.Bits(2)) counter_2 (.en(counter_1_ovf), .C(Clock), .clr(1'b0), .out(counter_2_out));  // open: ovf
  Decoder #(.Selector_Bits(2)) decoder_1 (
    .sel(counter_2_out), .out_0(decoder_1_out_0), .out_1(decoder_1_out_1), .out_2(decoder_1_out_2),
    .out_3(decoder_1_out_3));
  GraphicCard #(.graphicHeight(768), .graphicWidth(1024), .Bits(16)) graphiccard_1 (
    .A({1'b0, vga_sync_jarvi_1024x768_1_y_2, vga_sync_jarvi_1024x768_1_y, vga_sync_jarvi_1024x768_1_x_2[9:5], vga_sync_jarvi_1024x768_1_x}),
    .str(vga_sync_jarvi_1024x768_1_oe), .C(Clock), .ld(1'b0), .B(1'b0),
    .D({graphiccard_1_d, R3, R2, R1, R0, graphiccard_1_d_2[9], G3, G2, G1, G0, graphiccard_1_d_2[4], B3, B2, B1, B0}));
  or or_1 (or_1_out, decoder_1_out_2, decoder_1_out_3);
  D_FF d_ff_1 (.D(vga_sync_jarvi_1024x768_1_h_sync), .C(Clock), .Q(H_sync));  // open: nQ
  D_FF d_ff_2 (.D(vga_sync_jarvi_1024x768_1_v_sync), .C(Clock), .Q(V_sync));  // open: nQ
  ROM #(.AddrBits(10), .Bits(12)) rom_1 (
    .A({vga_sync_jarvi_1024x768_1_y, vga_sync_jarvi_1024x768_1_x}), .sel(or_1_out),
    .D({R3, R2, R1, R0, G3, G2, G1, G0, B3, B2, B1, B0}));
  ROM #(.AddrBits(10), .Bits(12)) rom_2 (
    .A({vga_sync_jarvi_1024x768_1_y, vga_sync_jarvi_1024x768_1_x}), .sel(decoder_1_out_1),
    .D({R3, R2, R1, R0, G3, G2, G1, G0, B3, B2, B1, B0}));
  ROM #(.AddrBits(10), .Bits(12)) rom_3 (
    .A({vga_sync_jarvi_1024x768_1_y, vga_sync_jarvi_1024x768_1_x}), .sel(decoder_1_out_0),
    .D({R3, R2, R1, R0, G3, G2, G1, G0, B3, B2, B1, B0}));
  // also tied to GND on the sheet: {graphiccard_1_d[0], graphiccard_1_d_2[9], graphiccard_1_d_2[4]}
  // also tied to VCC on the sheet: graphiccard_1_d[1]

  // Notes on the sheet:
  //   R0: pin G19
  //   G0: pin J17
  //   B0: pin N18
  //   R1: pin H19
  //   G1: pin H17
  //   B1: pin L18
  //   R2: pin J19
  //   G2: pin G17
  //   B2: pin K18
  //   R3: pin N19
  //   G3: pin D17
  //   B3: pin J18
  //   H_sync: pin P19
  //   V_sync: pin R19
  //   SW0: pin V17
  //   SW1: pin V16
  //   SW2: pin W16
  //   SW3: pin W17
  //   SW4: pin W15
  //   SW5: pin V15
  //   SW6: pin W14
  //   SW7: pin W13
  //   SW8: pin V2
  //   SW9: pin T3
  //   SW10: pin T2
  //   SW11: pin R3
  //   Clock: pin W5, Hz: 65000000
  //   Switches
  //   contents of rom_1 (hex, n*v repeats v):
  //   fff,fff,fff,fff,fff,fff,fff,fff,fff,fff,fff,fff,fff,fff,fff,fff,fff,fff,fff,fff,fff,
  //   fff,fff,fff,fff,fff,fff,fff,fff,fff,fff,fff,fff,fff,fff,fff,fff,fff,fff,fff,fff,fff,
  //   fff,fff,fff,fff,fff,fff,fff,fff,fff,fff,fff,fff,fff,fff,fff,fff,fff,fff,fff,fff,fff,
  //   fff,fff,fff,fff,fff,fff,fff,fff,fff,fff,fff,fff,fff,fff,fff,fff,fff,fff,fff,fff,fff,
  //   fff,fff,fff,fff,fff,fff,fff,fff,fff,fff,fff,fff,fff,fff,fff,fff,fff,fff,fff,fff,fff,
  //   fff,fff,fff,fff,fff,fff,fff,fff,fff,fff,fff,fff,fff,fff,fff,fff,fff,fff,fff,fff,fff,
  //   fff,fff,fff,fff,fff,fff,fff,fff,fff,fff,fff,fff,fff,fff,fff,fff,fff,fff,fff,fff,fff,
  //   fff,fff,fff,fff,fff,fff,fff,fff,fff,fff,fff,fff,fff,fff,fff,fff,fff,fff,0,0,0,0,0,
  //   0,0,fff,fff,fff,fff,fff,fff,fff,fff,0,0,0,0,0,0,0,fff,fff,fff,fff,fff,fff,fff,fff,
  //   fff,0,fff,fff,fff,fff,fff,fff,fff,0,fff,fff,fff,fff,fff,fff,0,fff,fff,fff,fff,fff,
  //   fff,fff,0,fff,fff,fff,fff,fff,fff,fff,0,fff,fff,fff,fff,fff,fff,fff,fff,fff,0,fff,
  //   fff,fff,fff,0,fff,fff,fff,fff,fff,fff,fff,fff,fff,0,fff,fff,fff,fff,fff,0,fff,fff,
  //   fff,fff,fff,fff,fff,fff,fff,fff,fff,0,fff,fff,0,fff,fff,fff,fff,fff,fff,fff,fff,fff,
  //   fff,fff,0,fff,fff,fff,fff,0,fff,fff,fff,fff,fff,fff,fff,fff,fff,fff,fff,fff,0,0,fff,
  //   fff,fff,fff,fff,fff,fff,fff,fff,fff,fff,fff,0,fff,fff,fff,fff,0,fff,fff,fff,fff,fff,
  //   fff,fff,fff,fff,fff,fff,fff,fff,fff,fff,fff,fff,fff,fff,fff,fff,fff,fff,fff,fff,fff,
  //   0,fff,fff,fff,fff,0,fff,fff,fff,fff,fff,fff,fff,fff,fff,fff,fff,fff,fff,fff,fff,fff,
  //   fff,fff,fff,fff,fff,fff,fff,fff,fff,fff,0,fff,fff,fff,fff,0,fff,fff,fff,fff,fff,fff,
  //   fff,fff,fff,fff,fff,fff,fff,fff,fff,fff,fff,fff,fff,fff,fff,fff,fff,fff,fff,fff,0,
  //   fff,fff,fff,fff,0,fff,fff,fff,fff,fff,fff,fff,fff,fff,fff,fff,fff,fff,fff,fff,fff,
  //   fff,fff,fff,fff,fff,fff,fff,fff,fff,fff,0,fff,fff,fff,fff,0,fff,fff,fff,fff,fff,fff,
  //   fff,fff,fff,fff,fff,fff,fff,fff,fff,fff,fff,fff,fff,fff,fff,fff,fff,fff,fff,fff,0,
  //   fff,fff,fff,fff,fff,0,fff,fff,fff,fff,fff,fff,fff,fff,fff,fff,fff,fff,fff,fff,fff,
  //   fff,fff,fff,fff,fff,fff,fff,fff,fff,0,fff,fff,fff,fff,fff,fff,fff,0,fff,fff,fff,fff,
  //   fff,fff,fff,fff,fff,fff,fff,fff,fff,fff,fff,fff,fff,fff,fff,fff,fff,fff,0,fff,fff,
  //   fff,fff,fff,fff,fff,fff,fff,0,fff,fff,fff,fff,fff,fff,fff,fff,fff,fff,fff,fff,fff,
  //   fff,fff,fff,fff,fff,fff,fff,0,fff,fff,fff,fff,fff,fff,fff,fff,fff,fff,fff,0,fff,fff,
  //   fff,fff,fff,fff,fff,fff,fff,fff,fff,fff,fff,fff,fff,fff,fff,fff,0,fff,fff,fff,fff,
  //   fff,fff,fff,fff,fff,fff,fff,fff,fff,0,fff,fff,fff,fff,fff,fff,fff,fff,fff,fff,fff,
  //   fff,fff,fff,fff,fff,0,fff,fff,fff,fff,fff,fff,fff,fff,fff,fff,fff,fff,fff,fff,fff,
  //   0,fff,fff,fff,fff,fff,fff,fff,fff,fff,fff,fff,fff,fff,fff,0,fff,fff,fff,fff,fff,fff,
  //   fff,fff,fff,fff,fff,fff,fff,fff,fff,fff,fff,0,fff,fff,fff,fff,fff,fff,fff,fff,fff,
  //   fff,fff,fff,0,fff,fff,fff,fff,fff,fff,fff,fff,fff,fff,fff,fff,fff,fff,fff,fff,fff,
  //   fff,fff,0,fff,fff,fff,fff,fff,fff,fff,fff,fff,fff,0,fff,fff,fff,fff,fff,fff,fff,fff,
  //   fff,fff,fff,fff,fff,fff,fff,fff,fff,fff,fff,fff,fff,0,fff,fff,fff,fff,fff,fff,fff,
  //   fff,0,fff,fff,fff,fff,fff,fff,fff,fff,fff,fff,fff,fff,fff,fff,fff,fff,fff,fff,fff,
  //   fff,fff,fff,fff,0,fff,fff,fff,fff,fff,fff,0,fff,fff,fff,fff,fff,fff,fff,fff,fff,fff,
  //   fff,fff,fff,fff,fff,fff,fff,fff,fff,fff,fff,fff,fff,fff,fff,0,fff,fff,fff,fff,0,fff,
  //   fff,fff,fff,fff,fff,fff,fff,fff,fff,fff,fff,fff,fff,fff,fff,fff,fff,fff,fff,fff,fff,
  //   fff,fff,fff,fff,fff,0,fff,fff,0,fff,fff,fff,fff,fff,fff,fff,fff,fff,fff,fff,fff,fff,
  //   fff,fff,fff,fff,fff,fff,fff,fff,fff,fff,fff,fff,fff,fff,fff,fff,0,0,fff,fff,fff,fff,
  //   fff,fff,fff,fff,fff,fff,fff,fff,fff,fff,fff,fff,fff,fff,fff,fff,fff,fff,fff,fff,fff,
  //   fff,fff,fff,fff,fff,fff,fff,fff,fff,fff,fff,fff,fff,fff,fff,fff,fff,fff,fff,fff,fff,
  //   fff,fff,fff,fff,fff,fff,fff,fff,fff,fff,fff,fff,fff,fff,fff,fff,fff,fff,fff,fff,fff,
  //   fff,fff,fff,fff,fff,fff,fff,fff,fff,fff,fff,fff,fff,fff,fff,fff,fff,fff,fff,fff,fff,
  //   fff,fff,fff,fff,fff,fff,fff,fff,fff,fff,fff,fff,fff,fff,fff,fff,fff,fff,fff,fff,fff,
  //   fff,fff,fff,fff,fff,fff,fff,fff,fff,fff,fff,fff,fff,fff,fff,fff,fff,fff,fff,fff,fff,
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  //   contents of rom_2 (hex, n*v repeats v):
  //   fff,fff,fff,fff,fff,fff,fff,fff,fff,fff,fff,fff,fff,fff,fff,fff,fff,fff,fff,fff,fff,
  //   fff,fff,fff,fff,fff,fff,fff,fff,fff,fff,fff,fff,fff,fff,fff,fff,fff,fff,fff,fff,fff,
  //   fff,fff,fff,fff,fff,fff,fff,fff,fff,fff,fff,fff,fff,fff,fff,fff,fff,fff,fff,fff,fff,
  //   fff,fff,fff,fff,fff,fff,fff,fff,fff,fff,fff,fff,fff,fff,fff,fff,fff,fff,fff,fff,fff,
  //   fff,fff,fff,fff,fff,fff,fff,fff,fff,fff,fff,fff,fff,fff,fff,fff,fff,fff,fff,fff,fff,
  //   fff,fff,fff,fff,fff,fff,fff,fff,fff,fff,fff,fff,fff,fff,fff,fff,fff,fff,fff,fff,fff,
  //   fff,fff,fff,fff,fff,fff,fff,fff,fff,fff,fff,fff,fff,fff,fff,fff,fff,fff,fff,fff,fff,
  //   fff,fff,fff,fff,fff,fff,fff,fff,fff,fff,fff,fff,fff,fff,fff,fff,fff,ffe,100,100,100,
  //   100,100,100,100,fff,fff,fff,fff,fff,fff,fff,fff,0,0,0,0,0,0,0,fff,fff,fff,fff,fff,
  //   fff,fff,fff,fff,100,500,820,920,910,910,920,720,200,fff,fff,fff,fff,fff,fff,0,fff,
  //   fff,fff,fff,fff,fff,fff,0,fff,fff,fff,fff,fff,fff,fff,100,722,820,c42,d41,d41,e31,
  //   e31,d42,821,200,ffe,fff,fff,fff,0,fff,fff,fff,fff,fff,fff,fff,fff,fff,0,fff,fff,fff,
  //   fff,fff,100,410,721,c43,fdb,d41,e31,e30,e31,e31,d32,c43,300,ffe,fff,0,fff,fff,fff,
  //   fff,fff,fff,fff,fff,fff,fff,fff,0,fff,fff,fff,fff,100,732,821,fdc,c42,d41,e30,f30,
  //   f31,f31,f31,d31,b42,200,0,fff,fff,fff,fff,fff,fff,fff,fff,fff,fff,fff,fff,0,fff,fff,
  //   fff,fff,200,721,821,fdc,d41,e30,e30,f30,e30,e30,e30,e31,d41,b53,ffe,fff,fff,fff,fff,
  //   fff,fff,fff,fff,fff,fff,fff,fff,0,fff,fff,fff,fff,200,721,820,c42,e41,e30,e30,f30,
  //   f30,f30,f30,e30,e30,c42,fee,fff,fff,fff,fff,fff,fff,fff,fff,fff,fff,fff,fff,0,fff,
  //   fff,fff,fff,200,721,910,d42,e31,e30,e30,e30,e30,e30,e30,e30,f30,c42,ffe,fff,fff,fff,
  //   fff,fff,fff,fff,fff,fff,fff,fff,fff,0,fff,fff,fff,fff,200,721,910,d41,e31,f31,e30,
  //   e30,e30,e30,f30,f30,e30,d42,ffe,fff,fff,fff,fff,fff,fff,fff,fff,fff,fff,fff,fff,0,
  //   fff,fff,fff,fff,100,410,810,d42,e31,f30,e30,f40,e30,f40,e30,f30,e31,c42,ffe,fff,fff,
  //   fff,fff,fff,fff,fff,fff,fff,fff,fff,fff,0,fff,fff,fff,fff,fff,100,721,910,e42,e31,
  //   f31,e30,e30,e30,e30,f30,e30,c42,ffe,fff,fff,fff,fff,fff,fff,fff,fff,fff,fff,fff,0,
  //   fff,fff,fff,fff,fff,fff,fff,100,500,910,d42,e31,e31,e31,e30,e30,f30,f30,c42,ffe,fff,
  //   fff,fff,fff,fff,fff,fff,fff,fff,fff,0,fff,fff,fff,fff,fff,fff,fff,fff,fff,200,821,
  //   910,d42,e31,e30,e30,f30,e30,f30,d42,ffe,fff,fff,fff,fff,fff,fff,fff,fff,fff,0,fff,
  //   fff,fff,fff,fff,fff,fff,fff,fff,fff,fff,200,500,910,d31,e41,e30,e30,f31,e30,d42,ffe,
  //   fff,fff,fff,fff,fff,fff,fff,fff,0,fff,fff,fff,fff,fff,fff,fff,fff,fff,fff,fff,fff,
  //   fff,100,821,a20,d31,e41,e30,e30,e30,d42,ffe,fff,fff,fff,fff,fff,fff,fff,0,fff,fff,
  //   fff,fff,fff,fff,fff,fff,fff,fff,fff,fff,fff,fff,fff,100,510,910,d31,e31,e30,f30,c42,
  //   ffe,fff,fff,fff,fff,fff,fff,0,fff,fff,fff,fff,fff,fff,fff,fff,fff,fff,fff,fff,fff,
  //   fff,fff,fff,fff,100,721,910,d31,e41,e30,c42,ffe,fff,fff,fff,fff,fff,0,fff,fff,fff,
  //   fff,fff,fff,fff,fff,fff,fff,fff,fff,fff,fff,fff,fff,fff,fff,fff,100,510,910,d41,e30,
  //   c42,ffe,fff,fff,fff,fff,0,fff,fff,fff,fff,fff,fff,fff,fff,fff,fff,fff,fff,fff,fff,
  //   fff,fff,fff,fff,fff,fff,fff,100,721,910,d42,c42,ffe,fff,fff,fff,0,fff,fff,fff,fff,
  //   fff,fff,fff,fff,fff,fff,fff,fff,fff,fff,fff,fff,fff,fff,fff,fff,fff,fff,fff,100,500,
  //   910,b43,ffe,fff,fff,0,fff,fff,fff,fff,fff,fff,fff,fff,fff,fff,fff,fff,fff,fff,fff,
  //   fff,fff,fff,fff,fff,fff,fff,fff,fff,fff,100,822,721,fff,fff,0,fff,fff,fff,fff,fff,
  //   fff,fff,fff,fff,fff,fff,fff,fff,fff,fff,fff,fff,fff,fff,fff,fff,fff,fff,fff,fff,fff,
  //   ffe,200,311,fff,0,fff,fff,fff,fff,fff,fff,fff,fff,fff,fff,fff,fff,fff,fff,fff,fff,
  //   fff,fff,fff,fff,fff,fff,fff,fff,fff,fff,fff,fff,fff,0,0,fff,fff,fff,fff,fff,fff,fff,
  //   fff,fff,fff,fff,fff,fff,fff,fff,fff,fff,fff,fff,fff,fff,fff,fff,fff,fff,fff,fff,fff,
  //   fff,fff,fff,fff,fff,fff,fff,fff,fff,fff,fff,fff,fff,fff,fff,fff,fff,fff,fff,fff,fff,
  //   fff,fff,fff,fff,fff,fff,fff,fff,fff,fff,fff,fff,fff,fff,fff,fff,fff,fff,fff,fff,fff,
  //   fff,fff,fff,fff,fff,fff,fff,fff,fff,fff,fff,fff,fff,fff,fff,fff,fff,fff,fff,fff,fff,
  //   fff,fff,fff,fff,fff,fff,fff,fff,fff,fff,fff,fff,fff,fff,fff,fff,fff,fff,fff,fff,fff,
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  //   contents of rom_3 (hex, n*v repeats v):
  //   fff,fff,fff,fff,fff,fff,fff,fff,fff,fff,fff,fff,fff,fff,fff,fff,fff,fff,fff,fff,fff,
  //   fff,fff,fff,fff,fff,fff,fff,fff,fff,fff,fff,fff,fff,fff,fff,fff,fff,fff,fff,fff,fff,
  //   fff,fff,fff,fff,fff,fff,fff,fff,fff,fff,fff,fff,fff,fff,fff,fff,fff,fff,fff,fff,fff,
  //   fff,fff,fff,fff,fff,fff,fff,fff,fff,fff,fff,fff,fff,fff,fff,fff,fff,fff,fff,fff,fff,
  //   fff,fff,fff,fff,fff,fff,fff,fff,fff,fff,fff,fff,fff,fff,fff,fff,fff,fff,fff,fff,fff,
  //   fff,fff,fff,fff,fff,fff,fff,fff,fff,fff,fff,fff,fff,fff,fff,fff,fff,fff,fff,fff,fff,
  //   fff,fff,fff,fff,fff,fff,fff,fff,fff,fff,fff,fff,fff,fff,fff,fff,fff,fff,fff,fff,fff,
  //   fff,fff,fff,fff,fff,fff,fff,fff,fff,fff,fff,fff,fff,fff,fff,fff,fff,fff,100,100,100,
  //   100,100,100,100,fff,fff,fff,fff,fff,fff,fff,fff,100,100,100,100,100,100,100,fff,fff,
  //   fff,fff,fff,fff,fff,fff,fff,200,500,820,920,920,920,920,720,200,fff,fff,fff,fff,fff,
  //   fff,200,820,920,920,920,920,821,500,200,fff,fff,fff,fff,fff,fff,fff,100,722,820,c42,
  //   d41,d31,e41,e31,d42,821,200,fff,fff,fff,ffe,200,821,d42,e31,e41,d31,d41,d42,910,722,
  //   100,fff,fff,fff,fff,fff,100,410,721,b43,fdc,d42,e31,e30,f30,f31,d41,c42,300,ffe,ffe,
  //   200,b42,d41,e41,e31,e31,e31,e31,e31,d41,820,410,100,fff,fff,fff,fff,100,722,820,fdc,
  //   c42,d32,e31,f30,f30,f30,f30,d41,b43,300,300,b43,d41,f40,e30,f31,f31,e31,e30,e31,e41,
  //   910,721,100,fff,fff,fff,fff,100,621,821,fdc,d42,e31,e31,e30,e30,e30,e30,e30,d41,d42,
  //   d42,d41,e31,e30,e30,e30,e31,e30,e30,e31,e31,910,821,200,fff,fff,fff,fff,200,722,820,
  //   c42,d31,f31,e31,e31,e30,e30,f40,e30,e30,e30,e30,e30,e31,f31,f30,f30,e31,e31,f30,e30,
  //   e31,a10,821,200,fff,fff,fff,fff,200,821,910,d42,e41,e30,e30,e31,e30,e30,e30,e30,f30,
  //   f30,f30,e30,e30,e30,e30,f30,f30,e30,f30,e30,e31,910,821,200,fff,fff,fff,fff,200,722,
  //   910,d42,e30,f30,f30,e30,e30,e30,f30,f30,e30,e30,e30,e30,e30,e40,e30,e30,f30,f30,e30,
  //   e30,e31,a10,721,100,fff,fff,fff,fff,100,410,810,d42,e30,f30,e30,f31,e30,f31,e30,f30,
  //   e30,e30,e30,f30,f30,e30,f31,e30,f30,e30,e40,e40,e42,910,400,100,fff,fff,fff,fff,fff,
  //   100,721,910,e41,e30,e30,e30,e31,e31,f30,f30,e30,f30,f31,e30,f30,f30,f30,f31,e30,e40,
  //   e40,d41,910,821,100,fff,fff,fff,fff,fff,fff,fff,100,500,910,d42,e31,e30,f31,e30,e30,
  //   f30,e30,f30,f31,f30,f30,e30,f30,f31,e30,e31,d41,910,500,100,fff,fff,fff,fff,fff,fff,
  //   fff,fff,fff,100,721,910,d42,e31,e30,e30,f30,e30,f31,e30,e30,f31,e30,f30,e30,e30,e31,
  //   d42,910,721,100,fff,fff,fff,fff,fff,fff,fff,fff,fff,fff,fff,200,500,910,d31,e30,f40,
  //   e30,e30,e30,f30,f30,e30,e30,e30,f40,e30,d31,910,500,200,fff,fff,fff,fff,fff,fff,fff,
  //   fff,fff,fff,fff,fff,fff,100,721,920,d41,e30,e41,e30,e30,f30,f30,e30,e30,e41,e30,d41,
  //   920,721,100,fff,fff,fff,fff,fff,fff,fff,fff,fff,fff,fff,fff,fff,fff,fff,100,500,910,
  //   d41,e30,e30,e30,f30,f30,e30,e30,e30,d41,910,500,100,fff,fff,fff,fff,fff,fff,fff,fff,
  //   fff,fff,fff,fff,fff,fff,fff,fff,fff,100,721,910,d41,e30,e30,e30,e30,e30,e30,d41,910,
  //   721,100,fff,fff,fff,fff,fff,fff,fff,fff,fff,fff,fff,fff,fff,fff,fff,fff,fff,fff,fff,
  //   100,510,910,e41,e31,e30,e30,e31,e41,910,510,100,fff,fff,fff,fff,fff,fff,fff,fff,fff,
  //   fff,fff,fff,fff,fff,fff,fff,fff,fff,fff,fff,fff,100,721,910,d41,e41,e41,d41,910,721,
  //   100,fff,fff,fff,fff,fff,fff,fff,fff,fff,fff,fff,fff,fff,fff,fff,fff,fff,fff,fff,fff,
  //   fff,fff,fff,100,500,910,d42,d42,910,500,100,fff,fff,fff,fff,fff,fff,fff,fff,fff,fff,
  //   fff,fff,fff,fff,fff,fff,fff,fff,fff,fff,fff,fff,fff,fff,fff,100,721,821,821,721,100,
  //   fff,fff,fff,fff,fff,fff,fff,fff,fff,fff,fff,fff,fff,fff,fff,fff,fff,fff,fff,fff,fff,
  //   fff,fff,fff,fff,fff,fff,200,410,410,200,fff,fff,fff,fff,fff,fff,fff,fff,fff,fff,fff,
  //   fff,fff,fff,fff,fff,fff,fff,fff,fff,fff,fff,fff,fff,fff,fff,fff,fff,fff,0,0,fff,fff,
  //   fff,fff,fff,fff,fff,fff,fff,fff,fff,fff,fff,fff,fff,fff,fff,fff,fff,fff,fff,fff,fff,
  //   fff,fff,fff,fff,fff,fff,fff,fff,fff,fff,fff,fff,fff,fff,fff,fff,fff,fff,fff,fff,fff,
  //   fff,fff,fff,fff,fff,fff,fff,fff,fff,fff,fff,fff,fff,fff,fff,fff,fff,fff,fff,fff,fff,
  //   fff,fff,fff,fff,fff,fff,fff,fff,fff,fff,fff,fff,fff,fff,fff,fff,fff,fff,fff,fff,fff,
  //   fff,fff,fff,fff,fff,fff,fff,fff,fff,fff,fff,fff,fff,fff,fff,fff,fff,fff,fff,fff,fff,
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  //   VGA
endmodule
